# Fritzing sketch Schematic_Sender_Module (saved by Fritzing 0.9.3b)
breadboards: 2

parts:
  BH1750 = BH1750
  U1 = LuaNode32 / ESP32
  BMP280 = BMP280 Breakout Board [part_number=BMP280]
  ZS-042_RTC_(DS3231) = ZS-042 RTC Module
  DHT22 = DHT22 module
  R1 = Photocell (LDR) [package=THT]
  R2 = Resistor [tolerance=±5% resistance=4.7k package=THT]
  ESP32_-_Back2 = ESP32 - CAM
  5V = Power plug

nets:
  VCC: BH1750.VCC, U1.3V3, BMP280.VCC, ZS-042_RTC_(DS3231).VCC, DHT22.VCC, R1.pin_1
  GND: BH1750.GND, U1.GND, BMP280.GND, ZS-042_RTC_(DS3231).GND, DHT22.GND, R2.Pin_0
  N1: BH1750.SCL, U1.D22, BMP280.SCL, ZS-042_RTC_(DS3231).SCL
  N2: BH1750.SDA, U1.D21, BMP280.SDA, ZS-042_RTC_(DS3231).SDA
  N3: U1.D33, DHT22.DATA
  N4: U1.D27, R1.pin_0, R2.Pin_1
  N5: ESP32_-_Back2.GND#7, 5V.GND
  5V: ESP32_-_Back2.5V, 5V.VCC

notes:
  Module 1 - Sender
  ESP32 board (30 pins)
  DHT22 - One-Wire - Temp. & Humidity
  BH1750 - I²C - Luximeter
  BMP280 - I²C - Temp. & Air Pressure
  DS3231 - I²C - Real Time Clock (RTC)
  Module 2: Receiver
  ESP32-CAM only
  --> Conected to the Wi-Fi network
  --> Receives data from the sender by ESP-NOW
  --> Hosts the web server.
  --> Saves the pictures taken in the MicroSD
  --> Saves the last picture in SPIFFS

custom parts:
  BH1750: Light Sensor
  LuaNode32 / ESP32: ESP32 based LuaNode32
  BMP280 Breakout Board: This is a breakout board for the Bosch Sensortec BMP280, "an absolute barometric pressure sensor especially designed for mobile applications." The operation range is 300 to 1100 hPa. Supply voltage is 1.2 to 3.6V. Operating temperature range is -40 to +85 °C.
  ESP32 - CAM: The ESP32-CAM has a very competitive small-size camera module that can operate independently as a minimum system with a footprint of only 27*40.5*4.5mm and a deep sleep current of up to 6mA.
